// Digital circuit GorkemYar_HW2.dig as structural Verilog
module GorkemYar_HW2 (
  input  in_1,
  input  in_2
);

  wire nor_1_out, not_1_out, not_2_out, not_3_out, not_4_out, or_1_out, or_2_out, or_3_out;

  not not_1 (not_1_out, in_2);
  or or_1 (or_1_out, not_1_out, in_2);
  not not_2 (not_2_out, in_1);
  not not_3 (not_3_out, in_1);
  or or_2 (or_2_out, not_3_out, in_2);
  not not_4 (not_4_out, in_2);
  or or_3 (or_3_out, in_1, not_4_out);
  nor nor_1 (nor_1_out, in_2, in_1);
  Seven_Seg seven_seg_1 (
    .a(or_2_out), .b(or_1_out), .c(or_3_out), .d(or_2_out), .e(not_2_out), .f(nor_1_out), .g(in_2), .dp(1'b0));
endmodule
