// Digital circuit down59n.dig as structural Verilog
module down59n (
  input  CLK,
  input  RESET,
  output [3:0] UNITS,
  output [3:0] TENS
);

  downcounter_new u_units (.EN(1'b1), .LOAD(1'b0), .IN(4'b0000), .CLK(CLK), .RESET(RESET), .CNT(UNITS));  // open: ZERO
  downcounter_new downcounter_new_1 (
    .EN(1'b1), .LOAD(1'b0), .IN(4'b0000), .CLK(CLK), .RESET(RESET), .CNT(TENS));  // open: ZERO
endmodule
