// Digital circuit down59testn.dig as structural Verilog
module down59testn (
  input  clk
);

  wire [3:0] down59_1_p2, down59_1_p3;

  // down59 down59_1: pin names not known; wires that end beside it: clk, down59_1_p2, down59_1_p3
  Seven_Seg_Hex seven_seg_hex_1 (.d(down59_1_p3), .dp(1'b0));
  Seven_Seg_Hex seven_seg_hex_2 (.d(down59_1_p2), .dp(1'b0));

  // Notes on the sheet:
  //   clk: Hz: 2
endmodule
