// Digital circuit project.dig as structural Verilog
module project (
  input  _1_kHz
);

  wire PRESET_out, RST_out, START_out, u_controller_countdown, u_controller_load, u_controller_start,
       u_counter_endd, u_downcounter_zero;
  wire [3:0] dipswitch_1_out, dipswitch_5_out, dipswitch_9_out, dipswitch_13_out, u_downcounter_m1,
       u_downcounter_m10, u_downcounter_s1, u_downcounter_s10;

  Button #(.activeLow("true")) RST (.out(RST_out));
  Seven_Seg_Hex seven_seg_hex_1 (.d(u_downcounter_m10), .dp(1'b0));
  DipSwitch dipswitch_1 (.out(dipswitch_1_out[3]));
  DipSwitch dipswitch_2 (.out(dipswitch_1_out[2]));
  DipSwitch dipswitch_3 (.out(dipswitch_1_out[1]));
  Seven_Seg_Hex seven_seg_hex_2 (.d(u_downcounter_m1), .dp(1'b1));
  downcounter #(.applicationType("IVERILOG")) u_downcounter (
    .rst(RST_out), .c1khz(_1_kHz), .count(u_controller_countdown), .load(u_controller_load),
    .pm10(dipswitch_1_out), .pm1(dipswitch_5_out), .ps10(dipswitch_9_out), .ps1(dipswitch_13_out),
    .m10(u_downcounter_m10), .m1(u_downcounter_m1), .s10(u_downcounter_s10), .s1(u_downcounter_s1),
    .zero(u_downcounter_zero));
  DipSwitch dipswitch_4 (.out(dipswitch_1_out[0]));
  DipSwitch dipswitch_5 (.out(dipswitch_5_out[3]));
  DipSwitch dipswitch_6 (.out(dipswitch_5_out[2]));
  Seven_Seg_Hex seven_seg_hex_3 (.d(u_downcounter_s10), .dp(1'b0));
  DipSwitch dipswitch_7 (.out(dipswitch_5_out[1]));
  DipSwitch dipswitch_8 (.out(dipswitch_5_out[0]));
  DipSwitch dipswitch_9 (.out(dipswitch_9_out[3]));
  Seven_Seg_Hex seven_seg_hex_4 (.d(u_downcounter_s1), .dp(1'b0));
  DipSwitch dipswitch_10 (.out(dipswitch_9_out[2]));
  DipSwitch dipswitch_11 (.out(dipswitch_9_out[1]));
  DipSwitch dipswitch_12 (.out(dipswitch_9_out[0]));
  DipSwitch dipswitch_13 (.out(dipswitch_13_out[3]));
  DipSwitch dipswitch_14 (.out(dipswitch_13_out[2]));
  DipSwitch dipswitch_15 (.out(dipswitch_13_out[1]));
  DipSwitch dipswitch_16 (.out(dipswitch_13_out[0]));
  controller #(.applicationType("IVERILOG")) u_controller (
    .clk(_1_kHz), .rst(RST_out), .beginn(START_out), .reset(PRESET_out), .zero(u_downcounter_zero),
    .endd(u_counter_endd), .load(u_controller_load), .start(u_controller_start),
    .countdown(u_controller_countdown));
  Button START (.out(START_out));
  Button PRESET (.out(PRESET_out));
  counter #(.applicationType("IVERILOG")) u_counter (
    .rst(RST_out), .clk(_1_kHz), .start(u_controller_start), .endd(u_counter_endd));

  // Notes on the sheet:
  //   _1_kHz: Hz: 1000
endmodule

/* Code of downcounter:
module downcounter(
    input rst, c1khz,
    input count, load,
    input [3:0] pm10,
    input [3:0] pm1,
    input [3:0] ps10,
    input [3:0] ps1,
    output reg [3:0] m10,
    output reg [3:0] m1,
    output reg [3:0] s10,
    output reg [3:0] s1,
    output zero);
   
 
 
  reg [3:0]min10;
  reg [3:0]min1;
  reg [3:0]sec10;
  reg [3:0]sec1;
 
  reg [0:0]zero_r;
 
  assign zero = (zero_r==1);

always @(posedge c1khz, negedge rst)

begin
if (~rst)
            begin
              zero_r <= 1;
              min10 <= 0;
              min1 <= 0;
              sec10 <= 0;
              sec1 <= 0;
            end

else if (load==1)
            begin
              zero_r <= 0;
	      if (pm10>=10)
		begin
		min10<=9;
                end
	      else
	      	begin
               	min10 <= pm10;
                end

              if (pm1>=10)
              	begin
              	min1 <= 9;
              	end
	      else
                begin
                min1<=pm1;
                end

	      if (ps10>=10)
                begin
                sec10<=5;
                end
	      else
                begin
                sec10 <= ps10;
                end

              if (ps1>=10)
                begin
                sec1<=9;
                end
              else
              	begin
              	sec1 <= ps1;
              	end
            end
m10 <= min10;
     m1 <= min1;
     s10 <= sec10;
     s1 <= sec1;
end

always @(posedge count)

begin
     if (sec1 != 0)
       begin
         sec1 <= sec1-1;
         zero_r <= 0;
       end
     else
       begin
         if (sec10 != 0)
           begin
             sec10 <= sec10-1;
             sec1 <= 9;
             zero_r <= 0;
           end
         else
           begin
             if (min1 != 0)
               begin
                 min1 <= min1-1;
                 sec10 <= 5;
                 sec1 <= 9;
                 zero_r <= 0;
               end
             else
               begin
                 if (min10 != 0)
                   begin
                     min10 <= min10-1;
                     min1 <= 9;
                     sec10 <= 5;
                     sec1 <= 9;
                     zero_r <= 0;
                   end
                 else
                   begin
                     zero_r <= 1;
                   end
               end
           end
       end
end

endmodule
*/

/* Code of controller:
module controller(
    input clk,
    input rst,
    input beginn, 
    input reset,
    input zero,
    input endd,
    output load,
    output start,
    output countdown
    );

  reg countTemp;
  
  reg startTemp2;
  reg startTemp;
  assign countdown=countTemp&& startTemp2;
  assign start= (startTemp2 && startTemp) ;
  assign load=reset;

always @(posedge clk, negedge rst)
begin
      if (~rst==1 | load==1)
      begin
	startTemp2 = 0;

	countTemp = 0;
	startTemp=0;
      end
else

 if(zero && beginn) // go to state zero if rese
        begin
          countTemp = 0;
	  startTemp2= 0;
	  startTemp=0;
        end
    else if (zero && ~beginn)
        begin 
          startTemp=0;  
          countTemp = 0;
	  startTemp2= 0;
        end
    
    else if (~zero && beginn)
        begin 
            countTemp = endd;
	    startTemp2 = 1;
            startTemp = 1;
        end
    
    else if (~zero && ~beginn)
        begin 
        startTemp = endd;
        countTemp = endd;
        end 
end
endmodule
*/

/* Code of counter:
module counter(
    input rst,
    input clk,
    input start,
    output endd);
    
    reg [9:0] cnt;
    
    assign endd = (cnt==0);
    
    always @(posedge clk, negedge rst)
    begin
        if (~rst)
        begin
            cnt <= 0;
        end
        else
        begin
            if (start)
                cnt <= 999;
            else if (~endd)
                cnt <= cnt-1;
        end
    end // always
endmodule
*/
